# Fritzing sketch motor-driver-esp32-conection (saved by Fritzing 1.0.0rc)
breadboards: 1

parts:
  M1 = DC Motor [voltage_(max)=6V voltage_(min)=3V]
  M2 = DC Motor [voltage_(max)=6V voltage_(min)=3V]
  Componente1 = Adafruit TB6612 DC and Stepper Motor Driver [part_number="Adafruit #2448"]  # not connected
  BAT1 = BC9VPC [package=bc9vpc]
  Componente2 = InvenSense MPU6050  # not connected
  S1 = Toggle Switch [package=THT]  # not connected
  F1 = FUSE [package=fuse_5mm]  # not connected
  Componente4 = Motor Driver 1A Dual TB6612FNG
  M3 = DOIT Esp32 DevKit v1 (30 pins long, 11 pins width) [part_number=ESP32S-PIN30]

nets:
  N1: M1.pin_1, Componente4.B01
  N2: M1.pin_2, Componente4.B02
  N3: M2.pin_1, Componente4.A02
  N4: M2.pin_2, Componente4.A01
  N5: BAT1.V+, Componente4.VM, M3.VIN
  GND: BAT1.V-, Componente4.GND, M3.GND
  VCC: Componente4.VCC, Componente4.STBY, M3.3V3
  N6: Componente4.PWMA, M3.D25
  N7: Componente4.AIN2, M3.D27
  N8: Componente4.AIN1, M3.D26
  N9: Componente4.BIN1, M3.D14
  N10: Componente4.BIN2, M3.D12
  N11: Componente4.PWMB, M3.D33

custom parts:
  Adafruit TB6612 DC and Stepper Motor Driver: Spin two DC motors, step one bi-polar or uni-polar stepper, or fire off two solenoids with 1.2A per channel using the TB6612. These are perhaps better known as "the drivers in our assembled Adafruit Motorshield or Motor HAT." We really like these dual H-bridges, so if you want to control motors without a shield or HAT these are easy to include on any solderless breadboard or perma-proto.
  DOIT Esp32 DevKit v1 (30 pins long, 11 pins width): The DOIT Esp32 DevKit v1 is one of the development board created by DOIT to evaluate the ESP-WROOM-32 module. It is based on the ESP32 microcontroller that boasts Wifi, Bluetooth, Ethernet and Low Power support all in a single chip. (vanepp) made breadboard work, adjusted pin numbering and labels and reduced size of schematic and cleaned up pcb. This chip is 30pins long (2 x15) and 11 pins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

// code stored in the sketch: motor-driver-esp32-conection.ino
// Pines del Motor A
const int PWMA = 25;
const int AIN1 = 26;
const int AIN2 = 27;

// Pines del Motor B
const int BIN1 = 14;
const int BIN2 = 12;
const int PWMB = 33;

void setup() {
  // Configurar todos los pines como salida
  pinMode(PWMA, OUTPUT);
  pinMode(AIN1, OUTPUT);
  pinMode(AIN2, OUTPUT);
  pinMode(BIN1, OUTPUT);
  pinMode(BIN2, OUTPUT);
  pinMode(PWMB, OUTPUT);
}

void loop() {
  // Motor A - Girar adelante a velocidad media/alta
  digitalWrite(AIN1, HIGH);
  digitalWrite(AIN2, LOW);
  analogWrite(PWMA, 200); // Valor entre 0 y 255

  // Motor B - Girar adelante a velocidad media/alta
  digitalWrite(BIN1, HIGH);
  digitalWrite(BIN2, LOW);
  analogWrite(PWMB, 200); 

  delay(3000); // Girar por 3 segundos

  // Detener ambos motores
  digitalWrite(AIN1, LOW);
  digitalWrite(AIN2, LOW);
  digitalWrite(BIN1, LOW);
  digitalWrite(BIN2, LOW);
  
  delay(2000); // Esperar 2 segundos antes de repetir
}
